// Logisim project lab4.circ as structural Verilog: 1 circuit, main circuit main
module main (
  input  a__8,
  input  b__4,
  input  c__2,
  input  d__1,
  input  a__8_2,
  input  b__4_2,
  input  c__2_2,
  input  d__1_2
);

  wire and_1_out, and_2_out, and_3_out, and_4_out, and_5_out, or_1_out, xnor_1_out, xnor_2_out;

  and and_1 (and_1_out, ~a__8, ~b__4, ~c__2, ~d__1);  // AND_Gate
  and and_2 (and_2_out, a__8, ~b__4, c__2, ~d__1);  // AND_Gate
  and and_3 (and_3_out, ~a__8, b__4, ~c__2, d__1);  // AND_Gate
  and and_4 (and_4_out, a__8, b__4, c__2, d__1);
  xnor xnor_1 (xnor_1_out, a__8_2, c__2_2);
  xnor xnor_2 (xnor_2_out, b__4_2, d__1_2);
  and and_5 (and_5_out, xnor_1_out, xnor_2_out);
  // Probe on or_1_out
  or or_1 (or_1_out, and_1_out, and_2_out, and_3_out, and_4_out);
  // Probe on and_5_out

  // Notes on the sheet:
  //   AND/OR Implementation
  //   XOR/AND Implementation
endmodule
