// Logisim project lab5.circ as structural Verilog: 1 circuit, main circuit main
module main (
  input  A,
  input  B,
  input  A0,
  input  A1,
  input  B0,
  input  B1
);

  wire and_1_out, and_2_out, and_3_out, and_4_out, and_5_out, and_6_out, and_7_out, and_8_out, and_9_out,
       or_1_out, or_2_out, xnor_1_out, xnor_2_out;

  and and_1 (and_1_out, ~A0, B0);  // AND_Gate
  and and_2 (and_2_out, A0, ~B0);  // AND_Gate
  // Probe on and_3_out
  and and_3 (and_3_out, ~A, B);  // AND_Gate
  // Probe on xnor_1_out
  xnor xnor_1 (xnor_1_out, A, B);
  // Probe on and_4_out
  and and_4 (and_4_out, A, ~B);  // AND_Gate
  and and_5 (and_5_out, ~A1, B1);  // AND_Gate
  and and_6 (and_6_out, A1, ~B1);  // AND_Gate
  or or_1 (or_1_out, and_1_out, and_5_out);
  and and_7 (and_7_out, ~and_1_out, xnor_2_out, ~and_2_out);  // AND_Gate
  xnor xnor_2 (xnor_2_out, A1, B1);
  or or_2 (or_2_out, and_6_out, and_2_out);
  and and_8 (and_8_out, or_1_out, ~and_2_out);  // AND_Gate
  // Probe on and_8_out
  // Probe on and_7_out
  // Probe on and_9_out
  and and_9 (and_9_out, ~and_1_out, or_2_out);  // AND_Gate

  // Notes on the sheet:
  //   1-bit
  //   2-bit
endmodule
